// Digital circuit 4bit_CPU.dig as structural Verilog
module _4bit_CPU (
  input  Clk,
  input  PCLoad,
  input  [3:0] PCDataIn,
  input  [3:0] RamDataIn,
  input  RamReadEnable,
  input  RamWriteEnable,
  input  CUEnable,
  output [3:0] RegisterWriteData
);

  wire and_1_out, cu_1_il, cu_1_rr1, cu_1_rr2, cu_1_we, cu_1_wreg, PC_p1, RAM_p1;
  wire [0:0] IR_p1;
  wire [1:0] not_1_out;
  wire [2:0] cu_1_alu;
  wire [3:0] alu_1_output, IR_p4, RAM_p6, registerfile_1_p7, registerfile_1_p8;

  // RAM RAM: pin names not known; wires that end beside it: RAM_p1, RamDataIn, Clk, RamReadEnable, RamWriteEnable, RAM_p6
  and and_1 (and_1_out, cu_1_alu[0], cu_1_alu[1], cu_1_alu[2]);
  // gp_register IR: pin names not known; wires that end beside it: {1'b0, IR_p1[0]}, RAM_p6, Clk, IR_p4
  // PC PC: pin names not known; wires that end beside it: PC_p1, PCLoad, PCDataIn, Clk, RAM_p1
  not not_1 (not_1_out[1], and_1_out);
  CU cu_1 (
    .Opcode(IR_p4), .Clk(Clk), .Enable(CUEnable), .RR1(cu_1_rr1), .RR2(cu_1_rr2), .WReg(cu_1_wreg),
    .WE(cu_1_we), .IL(cu_1_il), .ALU(cu_1_alu), .PCInc(PC_p1), .IF(IR_p1[0]));
  xor xor_1 (not_1_out[0], cu_1_il, and_1_out);
  Multiplexer #(.Selector_Bits(2), .Bits(4)) multiplexer_1 (
    .sel(not_1_out), .in_0(RAM_p6), .in_1(registerfile_1_p7), .in_2(alu_1_output), .in_3(4'b0000),
    .out(RegisterWriteData));
  // RegisterFile registerfile_1: pin names not known; wires that end beside it: cu_1_rr1, cu_1_rr2, cu_1_wreg, RegisterWriteData, cu_1_we, Clk, registerfile_1_p7, registerfile_1_p8
  ALU alu_1 (.A(registerfile_1_p7), .B(registerfile_1_p8), .Control(cu_1_alu), .Output(alu_1_output));  // open: Zero
endmodule
