// Digital circuit ALU.dig as structural Verilog
module ALU (
  input  [3:0] A,
  input  [3:0] B,
  input  [2:0] Control,
  output [3:0] Output,
  output Zero
);

  wire [3:0] _4bit_full_adder_1_p3, _4bit_subtractor_1_p4, and_1_p3, or_1_p3, slt_1_p3, xor_1_p3;

  // _4bit_full_adder _4bit_full_adder_1: pin names not known; wires that end beside it: A, B, _4bit_full_adder_1_p3
  // _4bit_subtractor _4bit_subtractor_1: pin names not known; wires that end beside it: A, B, 1'b0, _4bit_subtractor_1_p4
  // AND and_1: pin names not known; wires that end beside it: A, B, and_1_p3
  // OR or_1: pin names not known; wires that end beside it: A, B, or_1_p3
  // SLT slt_1: pin names not known; wires that end beside it: A, B, slt_1_p3
  // XOR xor_1: pin names not known; wires that end beside it: A, B, xor_1_p3
  Multiplexer #(.Selector_Bits(3), .Bits(4)) multiplexer_1 (
    .sel(Control), .in_0(_4bit_full_adder_1_p3), .in_1(_4bit_subtractor_1_p4), .in_2(and_1_p3),
    .in_3(or_1_p3), .in_4(xor_1_p3), .in_5(slt_1_p3), .in_6(4'b0000), .in_7(4'b0000), .out(Output));
  nor nor_1 (Zero, Output[0], Output[1], Output[2], Output[3]);
  Driver driver_1 ();  // open: in, en, out
endmodule
