// Digital circuit CU.dig as structural Verilog
module CU (
  input  [3:0] Opcode,
  input  Clk,
  input  Enable,
  output RR1,
  output RR2,
  output WReg,
  output WE,
  output IL,
  output [2:0] ALU,
  output PCInc,
  output IF
);

  wire and_1_out, and_2_out, and_3_out, and_4_out, and_5_out, and_6_out, and_7_out, and_8_out, and_10_out,
       LSB_q, MSB_q, not_1_out, not_2_out, not_3_out, not_4_out, not_5_out, not_6_out, not_7_out, not_8_out,
       not_9_out, not_10_out, not_11_out, not_12_out, not_13_out, or_1_out, or_2_out, or_3_out;

  and and_1 (and_1_out, MSB_q, not_1_out);
  not not_1 (not_1_out, Enable);
  and and_2 (and_2_out, Enable, LSB_q);
  or or_1 (or_1_out, and_1_out, and_2_out);
  and and_3 (and_3_out, not_2_out, not_3_out, Opcode[1]);
  not not_2 (not_2_out, Opcode[3]);
  not not_3 (not_3_out, Opcode[2]);
  and and_4 (and_4_out, not_4_out, not_5_out, not_6_out);
  not not_4 (not_4_out, Opcode[2]);
  not not_5 (not_5_out, Opcode[1]);
  not not_6 (not_6_out, Opcode[0]);
  or or_2 (or_2_out, Opcode[3], Opcode[1], Opcode[0]);
  and and_5 (and_5_out, not_7_out, not_8_out, Opcode[0]);
  not not_7 (not_7_out, Opcode[3]);
  not not_8 (not_8_out, Opcode[1]);
  and and_6 (and_6_out, not_9_out, Opcode[1], not_10_out);
  not not_9 (not_9_out, Opcode[3]);
  not not_10 (not_10_out, Opcode[0]);
  and and_7 (and_7_out, not_11_out, LSB_q);
  not not_11 (not_11_out, Enable);
  and and_8 (and_8_out, not_12_out, not_13_out, Enable);
  not not_12 (not_12_out, MSB_q);
  not not_13 (not_13_out, LSB_q);
  or or_3 (or_3_out, and_7_out, and_8_out);
  or or_4 (WReg, and_3_out, and_4_out);
  or or_5 (IL, and_5_out, and_6_out);
  D_FF MSB (.D(or_1_out), .C(Clk), .Q(MSB_q));  // open: nQ
  D_FF LSB (.D(or_3_out), .C(Clk), .Q(LSB_q));  // open: nQ
  Multiplexer #(.Selector_Bits(4), .Bits(3)) multiplexer_1 (
    .sel(Opcode), .in_0(3'b111), .in_1(3'b111), .in_2(3'b111), .in_3(3'b111), .in_4(3'b111), .in_5(3'b111),
    .in_6(3'b111), .in_7(3'b111), .in_8(3'b111), .in_9(3'b000), .in_10(3'b001), .in_11(3'b010),
    .in_12(3'b011), .in_13(3'b100), .in_14(3'b101), .in_15(3'b111), .out(ALU));
  nor nor_1 (IF, MSB_q, LSB_q);
  and and_9 (WE, or_2_out, MSB_q);
  and and_10 (and_10_out, IL, LSB_q);
  not not_14 (RR1, Opcode[3]);
  or or_6 (PCInc, MSB_q, and_10_out);

  assign RR2 = 1'b1;
endmodule
